// Logisim project contador-sincrono-16bit.circ as structural Verilog: 1 circuit, main circuit main
module main (
  input  CLK,
  input  CLEAR,
  output S0,
  output S1,
  output S2,
  output S3,
  output S4,
  output S5,
  output S6,
  output S7,
  output S2_2,
  output S3_2,
  output S4_2,
  output S5_2,
  output S6_2,
  output S7_2,
  output S6_3,
  output S7_3
);

  wire and_1_out, and_2_out, and_3_out, and_4_out, and_5_out, and_6_out, and_7_out, and_8_out, and_9_out,
       and_10_out, and_11_out, and_12_out, and_13_out, and_14_out, not_1_out;

  not not_1 (not_1_out, CLK);
  J_K_Flip_Flop j_k_ff_1 (.J(1'b1), .clk(not_1_out), .K(1'b1), .Q(S0), .reset(CLEAR));  // open: Qn, preset
  J_K_Flip_Flop j_k_ff_2 (.J(S0), .clk(not_1_out), .K(S0), .Q(S1), .reset(CLEAR));  // open: Qn, preset
  and and_1 (and_1_out, S1, S0);
  J_K_Flip_Flop j_k_ff_3 (.J(and_1_out), .clk(not_1_out), .K(and_1_out), .Q(S2), .reset(CLEAR));  // open: Qn, preset
  and and_2 (and_2_out, S2, and_1_out);
  J_K_Flip_Flop j_k_ff_4 (.J(and_2_out), .clk(not_1_out), .K(and_2_out), .Q(S3), .reset(CLEAR));  // open: Qn, preset
  and and_3 (and_3_out, S3, and_2_out);
  J_K_Flip_Flop j_k_ff_5 (.J(and_3_out), .clk(not_1_out), .K(and_3_out), .Q(S4), .reset(CLEAR));  // open: Qn, preset
  and and_4 (and_4_out, S4, and_3_out);
  J_K_Flip_Flop j_k_ff_6 (.J(and_4_out), .clk(not_1_out), .K(and_4_out), .Q(S5), .reset(CLEAR));  // open: Qn, preset
  and and_5 (and_5_out, S5, and_4_out);
  J_K_Flip_Flop j_k_ff_7 (.J(and_5_out), .clk(not_1_out), .K(and_5_out), .Q(S6), .reset(CLEAR));  // open: Qn, preset
  and and_6 (and_6_out, S6, and_5_out);
  J_K_Flip_Flop j_k_ff_8 (.J(and_6_out), .clk(not_1_out), .K(and_6_out), .Q(S7), .reset(CLEAR));  // open: Qn, preset
  and and_7 (and_7_out, S7, and_6_out);
  J_K_Flip_Flop j_k_ff_9 (.J(and_7_out), .clk(not_1_out), .K(and_7_out), .Q(S2_2), .reset(CLEAR));  // open: Qn, preset
  and and_8 (and_8_out, S2_2, and_7_out);
  J_K_Flip_Flop j_k_ff_10 (.J(and_8_out), .clk(not_1_out), .K(and_8_out), .Q(S3_2), .reset(CLEAR));  // open: Qn, preset
  and and_9 (and_9_out, S3_2, and_8_out);
  J_K_Flip_Flop j_k_ff_11 (.J(and_9_out), .clk(not_1_out), .K(and_9_out), .Q(S4_2), .reset(CLEAR));  // open: Qn, preset
  and and_10 (and_10_out, S4_2, and_9_out);
  J_K_Flip_Flop j_k_ff_12 (
    .J(and_10_out), .clk(not_1_out), .K(and_10_out), .Q(S5_2), .reset(CLEAR));  // open: Qn, preset
  and and_11 (and_11_out, S5_2, and_10_out);
  J_K_Flip_Flop j_k_ff_13 (
    .J(and_11_out), .clk(not_1_out), .K(and_11_out), .Q(S6_2), .reset(CLEAR));  // open: Qn, preset
  and and_12 (and_12_out, S6_2, and_11_out);
  J_K_Flip_Flop j_k_ff_14 (
    .J(and_12_out), .clk(not_1_out), .K(and_12_out), .Q(S7_2), .reset(CLEAR));  // open: Qn, preset
  and and_13 (and_13_out, S7_2, and_12_out);
  J_K_Flip_Flop j_k_ff_15 (
    .J(and_13_out), .clk(not_1_out), .K(and_13_out), .Q(S6_3), .reset(CLEAR));  // open: Qn, preset
  and and_14 (and_14_out, S6_3, and_13_out);
  J_K_Flip_Flop j_k_ff_16 (
    .J(and_14_out), .clk(not_1_out), .K(and_14_out), .Q(S7_3), .reset(CLEAR));  // open: Qn, preset
endmodule
