// Logisim project contador-sincrono-4bit.circ as structural Verilog: 1 circuit, main circuit main
module main (
  input  CLK,
  input  CLEAR,
  output S0,
  output S1,
  output S2,
  output S3
);

  wire and_1_out, and_2_out, not_1_out;

  not not_1 (not_1_out, CLK);
  J_K_Flip_Flop j_k_ff_1 (.J(1'b1), .clk(not_1_out), .K(1'b1), .Q(S0), .reset(CLEAR));  // open: Qn, preset
  J_K_Flip_Flop j_k_ff_2 (.J(S0), .clk(not_1_out), .K(S0), .Q(S1), .reset(CLEAR));  // open: Qn, preset
  and and_1 (and_1_out, S1, S0);
  J_K_Flip_Flop j_k_ff_3 (.J(and_1_out), .clk(not_1_out), .K(and_1_out), .Q(S2), .reset(CLEAR));  // open: Qn, preset
  and and_2 (and_2_out, S2, and_1_out);
  J_K_Flip_Flop j_k_ff_4 (.J(and_2_out), .clk(not_1_out), .K(and_2_out), .Q(S3), .reset(CLEAR));  // open: Qn, preset
endmodule
