// Logisim project contador-sincrono-8bit.circ as structural Verilog: 1 circuit, main circuit main
module main (
  input  CLK,
  input  CLEAR,
  output S0,
  output S1,
  output S2,
  output S3,
  output S4,
  output S5,
  output S6,
  output S7
);

  wire and_1_out, and_2_out, and_3_out, and_4_out, and_5_out, and_6_out, not_1_out;

  not not_1 (not_1_out, CLK);
  J_K_Flip_Flop j_k_ff_1 (.J(1'b1), .clk(not_1_out), .K(1'b1), .Q(S0), .reset(CLEAR));  // open: Qn, preset
  J_K_Flip_Flop j_k_ff_2 (.J(S0), .clk(not_1_out), .K(S0), .Q(S1), .reset(CLEAR));  // open: Qn, preset
  and and_1 (and_1_out, S1, S0);
  J_K_Flip_Flop j_k_ff_3 (.J(and_1_out), .clk(not_1_out), .K(and_1_out), .Q(S2), .reset(CLEAR));  // open: Qn, preset
  and and_2 (and_2_out, S2, and_1_out);
  J_K_Flip_Flop j_k_ff_4 (.J(and_2_out), .clk(not_1_out), .K(and_2_out), .Q(S3), .reset(CLEAR));  // open: Qn, preset
  and and_3 (and_3_out, S3, and_2_out);
  J_K_Flip_Flop j_k_ff_5 (.J(and_3_out), .clk(not_1_out), .K(and_3_out), .Q(S4), .reset(CLEAR));  // open: Qn, preset
  and and_4 (and_4_out, S4, and_3_out);
  J_K_Flip_Flop j_k_ff_6 (.J(and_4_out), .clk(not_1_out), .K(and_4_out), .Q(S5), .reset(CLEAR));  // open: Qn, preset
  and and_5 (and_5_out, S5, and_4_out);
  J_K_Flip_Flop j_k_ff_7 (.J(and_5_out), .clk(not_1_out), .K(and_5_out), .Q(S6), .reset(CLEAR));  // open: Qn, preset
  and and_6 (and_6_out, S6, and_5_out);
  J_K_Flip_Flop j_k_ff_8 (.J(and_6_out), .clk(not_1_out), .K(and_6_out), .Q(S7), .reset(CLEAR));  // open: Qn, preset
endmodule
