// Logisim project contador_sincrono_8bit_FF_tipo_T.circ as structural Verilog: 1 circuit, main circuit contadorSincrono_8bits
module contadorSincrono_8bits (
  input  CLK,
  input  CLR,
  output [7:0] OUTPUT
);

  wire and_1_out, and_2_out, and_3_out, and_4_out, and_5_out, and_6_out;

  T_Flip_Flop t_ff_1 (.clk(CLK), .T(1'b1), .Q(OUTPUT[0]), .reset(CLR));  // open: Qn, preset
  T_Flip_Flop t_ff_2 (.clk(CLK), .T(OUTPUT[0]), .Q(OUTPUT[1]), .reset(CLR));  // open: Qn, preset
  // Digital_Oscilloscope #(.nState(16)) digital_oscilloscope_1: pin names not known; wires that end beside it: CLK, OUTPUT[0], OUTPUT[1], OUTPUT[2], OUTPUT[3], OUTPUT[4], OUTPUT[5], OUTPUT[6], OUTPUT[7]
  and and_1 (and_1_out, OUTPUT[1], OUTPUT[0]);
  T_Flip_Flop t_ff_3 (.clk(CLK), .T(and_1_out), .Q(OUTPUT[2]), .reset(CLR));  // open: Qn, preset
  and and_2 (and_2_out, OUTPUT[2], and_1_out);
  T_Flip_Flop t_ff_4 (.clk(CLK), .T(and_2_out), .Q(OUTPUT[3]), .reset(CLR));  // open: Qn, preset
  and and_3 (and_3_out, OUTPUT[3], and_2_out);
  T_Flip_Flop t_ff_5 (.clk(CLK), .T(and_3_out), .Q(OUTPUT[4]), .reset(CLR));  // open: Qn, preset
  and and_4 (and_4_out, OUTPUT[4], and_3_out);
  T_Flip_Flop t_ff_6 (.clk(CLK), .T(and_4_out), .Q(OUTPUT[5]), .reset(CLR));  // open: Qn, preset
  and and_5 (and_5_out, OUTPUT[5], and_4_out);
  T_Flip_Flop t_ff_7 (.clk(CLK), .T(and_5_out), .Q(OUTPUT[6]), .reset(CLR));  // open: Qn, preset
  and and_6 (and_6_out, OUTPUT[6], and_5_out);
  T_Flip_Flop t_ff_8 (.clk(CLK), .T(and_6_out), .Q(OUTPUT[7]), .reset(CLR));  // open: Qn, preset
endmodule
