// Logisim project registrador-paralelo-com-set-16bit.circ as structural Verilog: 1 circuit, main circuit main
module main (
  input  PR0,
  input  PR1,
  input  PR2,
  input  PR3,
  input  PR4,
  input  PR5,
  input  PR6,
  input  PR7,
  input  PR8,
  input  PR9,
  input  PR10,
  input  PR11,
  input  PR12,
  input  PR13,
  input  PR14,
  input  PR15,
  input  ENABLE,
  input  SET,
  input  ENTRADA_SERIE,
  input  CLOCK,
  input  CLEAR,
  output S0,
  output S1,
  output S2,
  output S3,
  output S4,
  output S5,
  output S6,
  output S7,
  output S8,
  output S9,
  output S10,
  output S11,
  output S12,
  output S13,
  output S14,
  output S15
);

  wire and_1_out, and_2_out, and_3_out, and_4_out, and_5_out, and_6_out, and_7_out, and_8_out, and_9_out,
       and_10_out, and_11_out, and_12_out, and_13_out, and_14_out, and_15_out, and_16_out, and_17_out,
       nand_1_out, nand_2_out, nand_3_out, nand_4_out, nand_5_out, nand_6_out, nand_7_out, nand_8_out,
       nand_9_out, nand_10_out, nand_11_out, nand_12_out, nand_13_out, nand_14_out, nand_15_out, nand_16_out,
       not_1_out, not_2_out, not_3_out, not_4_out, not_5_out, not_6_out, not_7_out, not_8_out, not_9_out,
       not_10_out, not_11_out, not_12_out, not_13_out, not_14_out, not_15_out, not_16_out;

  and and_1 (and_1_out, SET, CLOCK);
  nand nand_1 (nand_1_out, PR0, ENABLE);
  not not_1 (not_1_out, nand_1_out);
  and and_2 (and_2_out, SET, not_1_out);
  D_Flip_Flop d_ff_1 (.clk(and_1_out), .D(ENTRADA_SERIE), .Q(S0), .preset(and_2_out), .reset(CLEAR));  // open: Qn
  nand nand_2 (nand_2_out, PR1, ENABLE);
  not not_2 (not_2_out, nand_2_out);
  and and_3 (and_3_out, SET, not_2_out);
  D_Flip_Flop d_ff_2 (.clk(and_1_out), .D(S0), .Q(S1), .preset(and_3_out), .reset(CLEAR));  // open: Qn
  nand nand_3 (nand_3_out, PR2, ENABLE);
  not not_3 (not_3_out, nand_3_out);
  and and_4 (and_4_out, SET, not_3_out);
  D_Flip_Flop d_ff_3 (.clk(and_1_out), .D(S1), .Q(S2), .preset(and_4_out), .reset(CLEAR));  // open: Qn
  nand nand_4 (nand_4_out, PR3, ENABLE);
  not not_4 (not_4_out, nand_4_out);
  and and_5 (and_5_out, SET, not_4_out);
  D_Flip_Flop d_ff_4 (.clk(and_1_out), .D(S2), .Q(S3), .preset(and_5_out), .reset(CLEAR));  // open: Qn
  nand nand_5 (nand_5_out, PR4, ENABLE);
  not not_5 (not_5_out, nand_5_out);
  and and_6 (and_6_out, SET, not_5_out);
  D_Flip_Flop d_ff_5 (.clk(and_1_out), .D(S3), .Q(S4), .preset(and_6_out), .reset(CLEAR));  // open: Qn
  nand nand_6 (nand_6_out, PR5, ENABLE);
  not not_6 (not_6_out, nand_6_out);
  and and_7 (and_7_out, SET, not_6_out);
  D_Flip_Flop d_ff_6 (.clk(and_1_out), .D(S4), .Q(S5), .preset(and_7_out), .reset(CLEAR));  // open: Qn
  nand nand_7 (nand_7_out, PR6, ENABLE);
  not not_7 (not_7_out, nand_7_out);
  and and_8 (and_8_out, SET, not_7_out);
  D_Flip_Flop d_ff_7 (.clk(and_1_out), .D(S5), .Q(S6), .preset(and_8_out), .reset(CLEAR));  // open: Qn
  nand nand_8 (nand_8_out, PR7, ENABLE);
  not not_8 (not_8_out, nand_8_out);
  and and_9 (and_9_out, SET, not_8_out);
  D_Flip_Flop d_ff_8 (.clk(and_1_out), .D(S6), .Q(S7), .preset(and_9_out), .reset(CLEAR));  // open: Qn
  nand nand_9 (nand_9_out, PR8, ENABLE);
  not not_9 (not_9_out, nand_9_out);
  and and_10 (and_10_out, SET, not_9_out);
  D_Flip_Flop d_ff_9 (.clk(and_1_out), .D(S7), .Q(S8), .preset(and_10_out), .reset(CLEAR));  // open: Qn
  nand nand_10 (nand_10_out, PR9, ENABLE);
  not not_10 (not_10_out, nand_10_out);
  and and_11 (and_11_out, SET, not_10_out);
  D_Flip_Flop d_ff_10 (.clk(and_1_out), .D(S8), .Q(S9), .preset(and_11_out), .reset(CLEAR));  // open: Qn
  nand nand_11 (nand_11_out, PR10, ENABLE);
  not not_11 (not_11_out, nand_11_out);
  and and_12 (and_12_out, SET, not_11_out);
  D_Flip_Flop d_ff_11 (.clk(and_1_out), .D(S9), .Q(S10), .preset(and_12_out), .reset(CLEAR));  // open: Qn
  nand nand_12 (nand_12_out, PR11, ENABLE);
  not not_12 (not_12_out, nand_12_out);
  and and_13 (and_13_out, SET, not_12_out);
  D_Flip_Flop d_ff_12 (.clk(and_1_out), .D(S10), .Q(S11), .preset(and_13_out), .reset(CLEAR));  // open: Qn
  nand nand_13 (nand_13_out, PR12, ENABLE);
  not not_13 (not_13_out, nand_13_out);
  and and_14 (and_14_out, SET, not_13_out);
  D_Flip_Flop d_ff_13 (.clk(and_1_out), .D(S11), .Q(S12), .preset(and_14_out), .reset(CLEAR));  // open: Qn
  nand nand_14 (nand_14_out, PR13, ENABLE);
  not not_14 (not_14_out, nand_14_out);
  and and_15 (and_15_out, SET, not_14_out);
  D_Flip_Flop d_ff_14 (.clk(and_1_out), .D(S12), .Q(S13), .preset(and_15_out), .reset(CLEAR));  // open: Qn
  nand nand_15 (nand_15_out, PR14, ENABLE);
  not not_15 (not_15_out, nand_15_out);
  and and_16 (and_16_out, SET, not_15_out);
  D_Flip_Flop d_ff_15 (.clk(and_1_out), .D(S13), .Q(S14), .preset(and_16_out), .reset(CLEAR));  // open: Qn
  nand nand_16 (nand_16_out, PR15, ENABLE);
  not not_16 (not_16_out, nand_16_out);
  and and_17 (and_17_out, SET, not_16_out);
  D_Flip_Flop d_ff_16 (.clk(and_1_out), .D(S14), .Q(S15), .preset(and_17_out), .reset(CLEAR));  // open: Qn
endmodule
