// Logisim project registrador-paralelo-com-set-4bit.circ as structural Verilog: 2 circuits, main circuit main
module main (
  input  PR0,
  input  PR1,
  input  PR2,
  input  PR3,
  input  ENABLE,
  input  SET,
  input  ENTRADA_SERIE,
  input  CLOCK,
  input  CLEAR,
  input  in_10,
  input  in_11,
  input  in_12,
  input  in_13,
  input  in_14,
  input  in_15,
  input  in_16,
  input  in_17,
  input  in_18,
  output S0,
  output S1,
  output S2,
  output S3
);

  wire and_1_out, and_2_out, and_3_out, and_4_out, and_5_out, nand_1_out, nand_2_out, nand_3_out, nand_4_out,
       not_1_out, not_2_out, not_3_out, not_4_out, registrador_paralelo_set_1_s0,
       registrador_paralelo_set_1_s1, registrador_paralelo_set_1_s2, registrador_paralelo_set_1_s3;

  and and_1 (and_1_out, SET, CLOCK);
  nand nand_1 (nand_1_out, PR0, ENABLE);
  not not_1 (not_1_out, nand_1_out);
  and and_2 (and_2_out, SET, not_1_out);
  D_Flip_Flop d_ff_1 (.clk(and_1_out), .D(ENTRADA_SERIE), .Q(S0), .preset(and_2_out), .reset(CLEAR));  // open: Qn
  registrador_paralelo_set registrador_paralelo_set_1 (
    .ENABLE(in_14), .SET(in_15), .ENTRADA_SERIE(in_16), .CLOCK(in_17), .CLEAR(in_18), .PR0(in_10),
    .S0(registrador_paralelo_set_1_s0), .PR1(in_11), .S1(registrador_paralelo_set_1_s1), .PR2(in_12),
    .S2(registrador_paralelo_set_1_s2), .PR3(in_13), .S3(registrador_paralelo_set_1_s3));
  LED led_1 (.in(registrador_paralelo_set_1_s0));
  LED led_2 (.in(registrador_paralelo_set_1_s1));
  LED led_3 (.in(registrador_paralelo_set_1_s2));
  LED led_4 (.in(registrador_paralelo_set_1_s3));
  nand nand_2 (nand_2_out, PR1, ENABLE);
  not not_2 (not_2_out, nand_2_out);
  and and_3 (and_3_out, SET, not_2_out);
  D_Flip_Flop d_ff_2 (.clk(and_1_out), .D(S0), .Q(S1), .preset(and_3_out), .reset(CLEAR));  // open: Qn
  nand nand_3 (nand_3_out, PR2, ENABLE);
  not not_3 (not_3_out, nand_3_out);
  and and_4 (and_4_out, SET, not_3_out);
  D_Flip_Flop d_ff_3 (.clk(and_1_out), .D(S1), .Q(S2), .preset(and_4_out), .reset(CLEAR));  // open: Qn
  nand nand_4 (nand_4_out, PR3, ENABLE);
  not not_4 (not_4_out, nand_4_out);
  and and_5 (and_5_out, SET, not_4_out);
  D_Flip_Flop d_ff_4 (.clk(and_1_out), .D(S2), .Q(S3), .preset(and_5_out), .reset(CLEAR));  // open: Qn
endmodule

module registrador_paralelo_set (
  input  PR0,
  input  PR1,
  input  PR2,
  input  PR3,
  input  ENABLE,
  input  SET,
  input  ENTRADA_SERIE,
  input  CLOCK,
  input  CLEAR,
  output S0,
  output S1,
  output S2,
  output S3
);

  wire and_1_out, and_2_out, and_3_out, and_4_out, and_5_out, nand_1_out, nand_2_out, nand_3_out, nand_4_out,
       not_1_out, not_2_out, not_3_out, not_4_out;

  and and_1 (and_1_out, SET, CLOCK);
  nand nand_1 (nand_1_out, PR0, ENABLE);
  not not_1 (not_1_out, nand_1_out);
  and and_2 (and_2_out, SET, not_1_out);
  D_Flip_Flop d_ff_1 (.clk(and_1_out), .D(ENTRADA_SERIE), .Q(S0), .preset(and_2_out), .reset(CLEAR));  // open: Qn
  nand nand_2 (nand_2_out, PR1, ENABLE);
  not not_2 (not_2_out, nand_2_out);
  and and_3 (and_3_out, SET, not_2_out);
  D_Flip_Flop d_ff_2 (.clk(and_1_out), .D(S0), .Q(S1), .preset(and_3_out), .reset(CLEAR));  // open: Qn
  nand nand_3 (nand_3_out, PR2, ENABLE);
  not not_3 (not_3_out, nand_3_out);
  and and_4 (and_4_out, SET, not_3_out);
  D_Flip_Flop d_ff_3 (.clk(and_1_out), .D(S1), .Q(S2), .preset(and_4_out), .reset(CLEAR));  // open: Qn
  nand nand_4 (nand_4_out, PR3, ENABLE);
  not not_4 (not_4_out, nand_4_out);
  and and_5 (and_5_out, SET, not_4_out);
  D_Flip_Flop d_ff_4 (.clk(and_1_out), .D(S2), .Q(S3), .preset(and_5_out), .reset(CLEAR));  // open: Qn
endmodule
