// Logisim project registrador-paralelo-com-set-8bit.circ as structural Verilog: 1 circuit, main circuit main
module main (
  input  PR0,
  input  PR1,
  input  PR2,
  input  PR3,
  input  PR4,
  input  PR5,
  input  PR6,
  input  PR7,
  input  ENABLE,
  input  SET,
  input  ENTRADA_SERIE,
  input  CLOCK,
  input  CLEAR,
  output S0,
  output S1,
  output S2,
  output S3,
  output S4,
  output S5,
  output S6,
  output S7
);

  wire and_1_out, and_2_out, and_3_out, and_4_out, and_5_out, and_6_out, and_7_out, and_8_out, and_9_out,
       nand_1_out, nand_2_out, nand_3_out, nand_4_out, nand_5_out, nand_6_out, nand_7_out, nand_8_out,
       not_1_out, not_2_out, not_3_out, not_4_out, not_5_out, not_6_out, not_7_out, not_8_out;

  and and_1 (and_1_out, SET, CLOCK);
  nand nand_1 (nand_1_out, PR0, ENABLE);
  not not_1 (not_1_out, nand_1_out);
  and and_2 (and_2_out, SET, not_1_out);
  D_Flip_Flop d_ff_1 (.clk(and_1_out), .D(ENTRADA_SERIE), .Q(S0), .preset(and_2_out), .reset(CLEAR));  // open: Qn
  nand nand_2 (nand_2_out, PR1, ENABLE);
  not not_2 (not_2_out, nand_2_out);
  and and_3 (and_3_out, SET, not_2_out);
  D_Flip_Flop d_ff_2 (.clk(and_1_out), .D(S0), .Q(S1), .preset(and_3_out), .reset(CLEAR));  // open: Qn
  nand nand_3 (nand_3_out, PR2, ENABLE);
  not not_3 (not_3_out, nand_3_out);
  and and_4 (and_4_out, SET, not_3_out);
  D_Flip_Flop d_ff_3 (.clk(and_1_out), .D(S1), .Q(S2), .preset(and_4_out), .reset(CLEAR));  // open: Qn
  nand nand_4 (nand_4_out, PR3, ENABLE);
  not not_4 (not_4_out, nand_4_out);
  and and_5 (and_5_out, SET, not_4_out);
  D_Flip_Flop d_ff_4 (.clk(and_1_out), .D(S2), .Q(S3), .preset(and_5_out), .reset(CLEAR));  // open: Qn
  nand nand_5 (nand_5_out, PR4, ENABLE);
  not not_5 (not_5_out, nand_5_out);
  and and_6 (and_6_out, SET, not_5_out);
  D_Flip_Flop d_ff_5 (.clk(and_1_out), .D(S3), .Q(S4), .preset(and_6_out), .reset(CLEAR));  // open: Qn
  nand nand_6 (nand_6_out, PR5, ENABLE);
  not not_6 (not_6_out, nand_6_out);
  and and_7 (and_7_out, SET, not_6_out);
  D_Flip_Flop d_ff_6 (.clk(and_1_out), .D(S4), .Q(S5), .preset(and_7_out), .reset(CLEAR));  // open: Qn
  nand nand_7 (nand_7_out, PR6, ENABLE);
  not not_7 (not_7_out, nand_7_out);
  and and_8 (and_8_out, SET, not_7_out);
  D_Flip_Flop d_ff_7 (.clk(and_1_out), .D(S5), .Q(S6), .preset(and_8_out), .reset(CLEAR));  // open: Qn
  nand nand_8 (nand_8_out, PR7, ENABLE);
  not not_8 (not_8_out, nand_8_out);
  and and_9 (and_9_out, SET, not_8_out);
  D_Flip_Flop d_ff_8 (.clk(and_1_out), .D(S6), .Q(S7), .preset(and_9_out), .reset(CLEAR));  // open: Qn
endmodule
