// Logisim project registrador-paralelo-serie-4bit.circ as structural Verilog: 1 circuit, main circuit main
module main (
  input  PR0,
  input  PR1,
  input  PR2,
  input  PR3,
  input  ENABLE,
  input  ENTRADA_SERIE,
  input  CLK,
  input  CLEAR,
  output S0,
  output S1,
  output S2,
  output S3
);

  wire nand_1_out, nand_2_out, nand_3_out, nand_4_out, not_1_out, not_2_out, not_3_out, not_4_out;

  nand nand_1 (nand_1_out, PR0, ENABLE);
  not not_1 (not_1_out, nand_1_out);
  D_Flip_Flop d_ff_1 (.clk(CLK), .D(ENTRADA_SERIE), .Q(S0), .preset(not_1_out), .reset(CLEAR));  // open: Qn
  nand nand_2 (nand_2_out, PR1, ENABLE);
  not not_2 (not_2_out, nand_2_out);
  D_Flip_Flop d_ff_2 (.clk(CLK), .D(S0), .Q(S1), .preset(not_2_out), .reset(CLEAR));  // open: Qn
  nand nand_3 (nand_3_out, PR2, ENABLE);
  not not_3 (not_3_out, nand_3_out);
  D_Flip_Flop d_ff_3 (.clk(CLK), .D(S1), .Q(S2), .preset(not_3_out), .reset(CLEAR));  // open: Qn
  nand nand_4 (nand_4_out, PR3, ENABLE);
  not not_4 (not_4_out, nand_4_out);
  D_Flip_Flop d_ff_4 (.clk(CLK), .D(S2), .Q(S3), .preset(not_4_out), .reset(CLEAR));  // open: Qn
endmodule
